// Logisim project ULA_8_BITS.circ as structural Verilog
module AND_8bits (
  input  [7:0] A,
  input  [7:0] B,
  output [7:0] \SAÍDA 
);

  and and_1 (\SAÍDA [0], B[0], A[0]);
  and and_2 (\SAÍDA [1], B[1], A[1]);
  and and_3 (\SAÍDA [2], B[2], A[2]);
  and and_4 (\SAÍDA [3], B[3], A[3]);
  and and_5 (\SAÍDA [4], B[4], A[4]);
  and and_6 (\SAÍDA [5], B[5], A[5]);
  and and_7 (\SAÍDA [6], B[6], A[6]);
  and and_8 (\SAÍDA [7], B[7], A[7]);
endmodule

module OR_8bits (
  input  [7:0] A,
  input  [7:0] B,
  output [7:0] \SAÍDA 
);

  or or_1 (\SAÍDA [0], B[0], A[0]);
  or or_2 (\SAÍDA [1], B[1], A[1]);
  or or_3 (\SAÍDA [2], B[2], A[2]);
  or or_4 (\SAÍDA [3], B[3], A[3]);
  or or_5 (\SAÍDA [4], B[4], A[4]);
  or or_6 (\SAÍDA [5], B[5], A[5]);
  or or_7 (\SAÍDA [6], B[6], A[6]);
  or or_8 (\SAÍDA [7], B[7], A[7]);
endmodule

module NOT_8bits (
  input  [7:0] A,
  output [7:0] \SAÍDA 
);

  assign \SAÍDA  = ~A;  // NOT_Gate not_1, 8 bits wide
endmodule

module NOR_8bits (
  input  [7:0] A,
  input  [7:0] B,
  output [7:0] \SAÍDA 
);

  nor nor_1 (\SAÍDA [0], B[0], A[0]);
  nor nor_2 (\SAÍDA [1], B[1], A[1]);
  nor nor_3 (\SAÍDA [2], B[2], A[2]);
  nor nor_4 (\SAÍDA [3], B[3], A[3]);
  nor nor_5 (\SAÍDA [4], B[4], A[4]);
  nor nor_6 (\SAÍDA [5], B[5], A[5]);
  nor nor_7 (\SAÍDA [6], B[6], A[6]);
  nor nor_8 (\SAÍDA [7], B[7], A[7]);
endmodule

module NAND_8bits (
  input  [7:0] A,
  input  [7:0] B,
  output [7:0] \SAÍDA 
);

  nand nand_1 (\SAÍDA [0], B[0], A[0]);
  nand nand_2 (\SAÍDA [1], B[1], A[1]);
  nand nand_3 (\SAÍDA [2], B[2], A[2]);
  nand nand_4 (\SAÍDA [3], B[3], A[3]);
  nand nand_5 (\SAÍDA [4], B[4], A[4]);
  nand nand_6 (\SAÍDA [5], B[5], A[5]);
  nand nand_7 (\SAÍDA [6], B[6], A[6]);
  nand nand_8 (\SAÍDA [7], B[7], A[7]);
endmodule

module XOR_8bits (
  input  [7:0] A,
  input  [7:0] B,
  output [7:0] \SAÍDA 
);

  xor xor_1 (\SAÍDA [0], B[0], A[0]);
  xor xor_2 (\SAÍDA [1], B[1], A[1]);
  xor xor_3 (\SAÍDA [2], B[2], A[2]);
  xor xor_4 (\SAÍDA [3], B[3], A[3]);
  xor xor_5 (\SAÍDA [4], B[4], A[4]);
  xor xor_6 (\SAÍDA [5], B[5], A[5]);
  xor xor_7 (\SAÍDA [6], B[6], A[6]);
  xor xor_8 (\SAÍDA [7], B[7], A[7]);
endmodule

module MUX_10x1 (
  input  [3:0] in_1,
  input  in_2,
  input  in_3,
  output out_4
);

  MULTIPLEXADOR_4_1 multiplexador_4_1_1 (
    .E0(in_1[0]), .E2(in_1[2]), .E1(in_1[1]), .S0(in_2), .E3(in_1[3]), .S1(in_3), .S(out_4));
endmodule
