// Logisim project flip_flop_jk.circ as structural Verilog: 2 circuits, main circuit main
module main (
  input  j,
  input  k,
  output Q,
  output minus_Q
);

  wire clock_1_out;

  Clock clock_1 (.out(clock_1_out));
  flip_flop_jk flip_flop_jk_1 (.k(k), .clock(clock_1_out), .j(j), .q(Q), .minus_q(minus_Q));
endmodule

module flip_flop_jk (
  input  k,
  input  clock,
  input  j,
  output q,
  output minus_q
);

  wire nand_1_out, nand_2_out;

  nand nand_1 (nand_1_out, k, q);
  nand nand_2 (nand_2_out, minus_q, j);
  S_R_Flip_Flop s_r_ff_1 (.S(nand_1_out), .clk(clock), .R(nand_2_out), .Q(q), .Qn(minus_q));  // open: preset, reset, en
endmodule
