// Logisim project memoria_rom.circ as structural Verilog
module ROM_memoria (
  input  [1:0] in_1,
  output [3:0] out_2
);

  Multiplexer #(.select(3), .width(8)) multiplexer_1 ();  // open: in0, in1, in2, in3, in4, in5, in6, in7, out, sel, en
  Multiplexer #(.select(2), .width(4)) multiplexer_2 (
    .in0(4'b0010), .in1(4'b0011), .in2(4'b0100), .in3(4'b1000), .out(out_2), .sel(in_1));  // open: en
endmodule
