// Logisim project otimizacao_logica.circ as structural Verilog: 1 circuit, main circuit main
module main (
  input  A,
  input  B,
  output out_3,
  output out_4
);

  wire and_1_out, and_2_out, not_1_out, not_2_out;

  not not_1 (not_1_out, B);
  not not_2 (not_2_out, A);
  xor xor_1 (out_4, A, B);
  and and_1 (and_1_out, A, not_1_out);
  and and_2 (and_2_out, not_2_out, B);
  or or_1 (out_3, and_1_out, and_2_out);

  // Notes on the sheet:
  //   circuito simplificado
  //   circuito original
endmodule
