// Logisim project shift.circ as structural Verilog
module shift_2 (
  input  [7:0] entrada,
  output [7:0] LEFT,
  output [7:0] RIGHT
);


  assign LEFT = {entrada[5:0], 2'b00};
  assign RIGHT = {2'b00, entrada[7:2]};
endmodule
